# Fritzing sketch _1_over_x (saved by Fritzing 0.9.1b)
circuit board: 8.46667cm x 5.64444cm
breadboards: 1

parts:
  Part1 = Arduino Uno (Rev3)
  R1 = Resistor [tolerance=±5% resistance=330 package=THT]
  LED1 = LED - 5mm [color="Green (565nm)" package="5 mm [THT]"]
  LED2 = LED - 5mm [color="Red (633nm)" package="5 mm [THT]"]
  R2 = Resistor [tolerance=±5% resistance=330 package=THT]

nets:
  N1: Part1.D9_PWM, R1.Pin_1
  N2: Part1.GND, LED1.cathode, LED2.cathode
  N3: Part1.D6_PWM, R2.Pin_1
  N4: R1.Pin_0, LED1.anode
  N5: LED2.anode, R2.Pin_0

// code stored in the sketch: _1_over_x.ino
const int leds[2] = { 6, 9 };      // the number of the LED pins

void setup() {
  pinMode(leds[0], OUTPUT);      
  pinMode(leds[1], OUTPUT);   
}

void loop()
{
  unsigned long currentMillis = millis();
  
  if (currentMillis != 7000) {
    int voltage = 127+ 128*sin(50000.0/(currentMillis-7000.0));
    analogWrite(leds[0], voltage);
    
    // The second LED is optional
    analogWrite(leds[1], 255-voltage);
  }
}
