# Fritzing sketch morse (saved by Fritzing 0.9.1b)
circuit board: 8.46667cm x 5.64444cm
breadboards: 1

parts:
  Part1 = Arduino Uno (Rev3)
  LED2 = LED - 5mm [color="Red (633nm)" package="5 mm [THT]"]
  R2 = Resistor [tolerance=±5% resistance=330 package=THT]

nets:
  N1: Part1.GND, LED2.cathode
  N2: Part1.D6_PWM, R2.Pin_1
  N3: LED2.anode, R2.Pin_0

// code stored in the sketch: _1_over_x.ino
const int leds[2] = { 6, 9 };      // the number of the LED pins

void setup() {
  pinMode(leds[0], OUTPUT);      
  pinMode(leds[1], OUTPUT);   
}

void loop()
{
  unsigned long currentMillis = millis();
  
  if (currentMillis != 7000) {
    int voltage = 127+ 128*sin(50000.0/(currentMillis-7000.0));
    analogWrite(leds[0], voltage);
    
    // The second LED is optional
    analogWrite(leds[1], 255-voltage);
  }
}

// code stored in the sketch: morse.ino
const int morseDelay = 75;

const unsigned char letters[26][4] = {
  { 1, 3, 0, 0 },
  { 3, 1, 1, 1 },
  { 3, 1, 3, 1 },
  { 3, 1, 1, 0 },
  { 1, 0, 0, 0 },
  { 1, 1, 3, 1 },
  { 3, 3, 1, 0 },
  { 1, 1, 1, 1 },
  { 1, 1, 0, 0 },
  { 1, 3, 3, 3 },
  { 3, 1, 3, 0 },
  { 1, 3, 1, 1 },
  { 3, 3, 0, 0 },
  { 3, 1, 0, 0 },
  { 3, 3, 3, 0 },
  { 1, 3, 3, 1 },
  { 3, 3, 1, 3 },
  { 1, 3, 1, 0 },
  { 1, 1, 1, 0 },
  { 3, 0, 0, 0 },
  { 1, 1, 3, 0 },
  { 1, 1, 1, 3 },
  { 1, 3, 3, 0 },
  { 3, 1, 1, 3 },
  { 3, 1, 3, 3 },
  { 3, 3, 1, 1 }
};
  
const int led = 6;

void setup() {
  Serial.begin(9600);

  pinMode(led, OUTPUT);	
}

void loop() {
  if (Serial.available() > 0) {
    int inByte = Serial.read();

    // Convert to upper case
    if (inByte >= 97 && inByte <= 122) {
      inByte -= 32; 
    }

    if (inByte == 32) { // space
      delay(4 * morseDelay);
    } else if (inByte >= 65 && inByte <= 90) { // letter
      const unsigned char* morse = letters[inByte-65];

      for (int i = 0; i < 4; ++i) {
        if (morse[i] == 0) {
          break;
        } 

        digitalWrite(led, HIGH);
        delay(morse[i] * morseDelay);
        digitalWrite(led, LOW);
        delay(morseDelay);
      }
    } else if (inByte >= 48 && inByte <= 57) { // number
      char number = (inByte - 39)%10 + 1;

      for (int i = 0; i < 5; ++i) {
        const char code = ((1 + 2*(((10+(number+number/6)-i)%11)/6)));

        digitalWrite(led, HIGH);
        delay(code * morseDelay);
        digitalWrite(led, LOW);
        delay(morseDelay);
      }
    }
    
    // The space between letters is three units
    delay(2 * morseDelay);
  }
}
